// Logisim project BigASM.circ as structural Verilog
module BOARD_BIG_ASM (
  output out_1
);

  wire button_1_out, CLK, CLR, d_ff_1_q, not_1_out, Write, Write_ASCII;
  wire [6:0] ASCII;
  wire [7:0] counter_1_q;
  wire [23:0] Dir_INPUT, Dir_MEMORY;
  wire [31:0] INPUT, MEMORY_IN, MEMORY_OUT;

  Button button_1 (.out(button_1_out));
  Clock clock_1 (.out(CLK));
  D_Flip_Flop d_ff_1 (.clk(CLK), .D(1'b1), .Q(d_ff_1_q), .reset(button_1_out));  // open: Qn, preset, en
  D_Flip_Flop d_ff_2 (.clk(CLK), .D(d_ff_1_q), .Qn(CLR), .reset(button_1_out));  // open: Q, preset, en
  BIG_ASM big_asm_1 (
    .DATA_INPUT(INPUT), .MEMORY_IN(MEMORY_OUT), .CLK(CLK), .CLR(CLR), .DIR_INPUT(Dir_INPUT),
    .MEMORY_OUT(MEMORY_IN), .DIR_MEMORY(Dir_MEMORY), .Write_OUTPUT(Write), .ASCII(ASCII),
    .Write_ASCII(Write_ASCII), .END(out_1));
  MEMORY memory_1 (.DIR(Dir_MEMORY), .DATA_IN(MEMORY_IN), .WRITE(Write), .CLK(CLK), .CLR(CLR), .DATA_OUT(MEMORY_OUT));
  INPUT input_1 (.DIR(Dir_INPUT), .CLK(CLK), .DATA_OUT(INPUT));
  Counter counter_1 (.load(1'b0), .count(not_1_out), .Q(counter_1_q), .clk(CLK), .clr(CLR));  // open: D, carry
  not not_1 (not_1_out, out_1);
  // Probe on INPUT
  // Probe on counter_1_q
  TTY #(.rows(32), .cols(60)) tty_1 (.data(ASCII), .clk(CLK), .we(Write_ASCII), .clr(CLR));

  // Other names for the same wires on the sheet: END = out_1

  // Notes on the sheet:
  //   COUNTER
  //   BOARD
endmodule

module INPUT (
  input  [23:0] DIR,
  input  CLK,
  output [31:0] DATA_OUT
);

  RAM #(.addrWidth(24), .dataWidth(32)) ram_1 (.addr(DIR), .data(DATA_OUT), .clk(CLK), .ld(1'b1));  // open: sel, clr
endmodule

module MEMORY (
  input  [23:0] DIR,
  input  [31:0] DATA_IN,
  input  WRITE,
  input  CLK,
  input  CLR,
  output [31:0] DATA_OUT
);

  wire not_1_out;

  not not_1 (not_1_out, WRITE);
  RAM #(.addrWidth(24), .dataWidth(32), .bus("separate")) ram_1 (
    .addr(DIR), .din(DATA_IN), .data(DATA_OUT), .clk(CLK), .ld(not_1_out), .clr(CLR));  // open: str, sel
endmodule

module BIG_ASM (
  input  [31:0] DATA_INPUT,
  input  [31:0] MEMORY_IN,
  input  CLR,
  input  CLK,
  output [23:0] DIR_INPUT,
  output [31:0] MEMORY_OUT,
  output [6:0] ASCII,
  output [23:0] DIR_MEMORY,
  output Write_OUTPUT,
  output END,
  output Write_ASCII
);

  wire cu_1_l_a, cu_1_l_b, cu_1_l_c, cu_1_l_d, cu_1_l_m, cu_1_l_n, cu_1_l_temp, cu_1_l_x, cu_1_l_y,
       cu_1_s_temp, cu_1_s_x, cu_1_s_y, end_t, or_2_out, print_dec_1_end, S0, S1, wait_2_q, Write_ASCII0,
       y__0;
  wire [1:0] cu_1_s_dir;
  wire [6:0] ASCII1, ASCII2;
  wire [31:0] m, n;

  CU cu_1 (
    .reset(CLR), .start(1'b1), .clk(CLK), .y__0(y__0), .L_temp(cu_1_l_temp), .S_temp(cu_1_s_temp),
    .L_a(cu_1_l_a), .L_b(cu_1_l_b), .L_c(cu_1_l_c), .L_d(cu_1_l_d), .L_x(cu_1_l_x), .L_y(cu_1_l_y),
    .S_x(cu_1_s_x), .S_y(cu_1_s_y), .L_m(cu_1_l_m), .L_n(cu_1_l_n), .out_6(end_t), .S_Dir(cu_1_s_dir));
  Data_path data_path_1 (
    .IOUT(DATA_INPUT), .L_temp(cu_1_l_temp), .S_temp(cu_1_s_temp), .CLK(CLK), .L_a(cu_1_l_a), .L_b(cu_1_l_b),
    .L_c(cu_1_l_c), .L_d(cu_1_l_d), .L_x(cu_1_l_x), .L_y(cu_1_l_y), .S_x(cu_1_s_x), .S_y(cu_1_s_y),
    .S_Dir(cu_1_s_dir), .L_m(cu_1_l_m), .L_n(cu_1_l_n), .DirInput(DIR_INPUT), .y__0(y__0), .out_19(m),
    .out_20(n));  // open: CLR
  // Probe on m
  // Probe on n
  or or_1 (Write_ASCII, Write_ASCII0, S0, S1);
  PRINT_DEC print_dec_1 (
    .num(n), .start(end_t), .CLK(CLK), .RST(CLR), .ASCII(ASCII1), .Write_ASCII(Write_ASCII0),
    .END(print_dec_1_end));
  Multiplexer #(.select(2), .width(7)) multiplexer_1 (
    .in0(ASCII1), .in1(7'b0101100), .in2(ASCII2), .out(ASCII), .sel({S1, S0}));  // open: in3, en
  D_Flip_Flop \wait  (.clk(CLK), .D(print_dec_1_end), .Q(S0), .reset(CLR));  // open: Qn, preset, en
  PRINT_DEC print_dec_2 (.num(m), .start(S0), .CLK(CLK), .RST(CLR), .ASCII(ASCII2), .Write_ASCII(S1), .END(END));
  or or_2 (or_2_out, END, wait_2_q);
  D_Flip_Flop wait_2 (.clk(CLK), .D(or_2_out), .Q(wait_2_q), .reset(CLR));  // open: Qn, preset, en

  // Other names for the same wires on the sheet: Write_ASCII1 = S0; Write_ASCII2 = S1
endmodule

module PRINT_UDEC (
  input  [31:0] num,
  input  start,
  input  CLK,
  input  RST,
  output [6:0] ASCII,
  output Write_ASCII,
  output \end 
);

  wire _0_c, _0_n, demultiplexer_1_out0, demultiplexer_2_out0, demultiplexer_2_out1, demultiplexer_3_out0,
       demultiplexer_3_out1, IDLE_2_q, IDLE_3_q, IDLE_4_q, IDLE_q, Lc, Lc_0, Ln, Ln_0, or_1_out;
  wire [23:0] bit_extender_1_out;
  wire [31:0] c, c___1, c___1_t, divider_1_rem, memory_1_data_out, multiplexer_1_out, multiplexer_2_out,
       multiplexer_3_out, n, n___10, n___10___48;

  Multiplexer #(.width(32), .enable("false")) multiplexer_1 (
    .in0(num), .in1(n___10), .out(multiplexer_1_out), .sel(Lc_0));
  Divider #(.width(32)) divider_1 (.a(n), .b(32'ha), .out(n___10), .rem(divider_1_rem));  // open: upper
  Adder #(.width(32)) adder_1 (.a(divider_1_rem), .b(32'h30), .out(n___10___48));  // open: cin, cout
  or or_1 (or_1_out, demultiplexer_1_out0, \end );
  Register #(.width(32)) u_n (.D(multiplexer_1_out), .en(Ln), .Q(n), .clk(CLK), .clr(RST));
  D_Flip_Flop IDLE (.clk(CLK), .D(or_1_out), .Q(IDLE_q), .preset(RST));  // open: Qn, en, reset
  Demultiplexer #(.enable("false")) demultiplexer_1 (
    .out0(demultiplexer_1_out0), .out1(Ln_0), .in(IDLE_q), .sel(start));
  or or_2 (Write_ASCII, demultiplexer_3_out0, demultiplexer_2_out1);
  Multiplexer #(.width(32), .enable("false")) multiplexer_2 (
    .in0(c___1), .in1(c___1_t), .out(multiplexer_2_out), .sel(Write_ASCII));
  Adder #(.width(32)) adder_2 (.a(c), .b(32'h1), .out(c___1));  // open: cin, cout
  Subtractor #(.width(32)) subtractor_1 (.a(c), .b(32'h1), .out(c___1_t));  // open: bin, bout
  D_Flip_Flop IDLE_2 (.clk(CLK), .D(Ln_0), .Q(IDLE_2_q), .reset(RST));  // open: Qn, preset, en
  Register #(.width(32)) u_c (.D(multiplexer_2_out), .en(Lc), .Q(c), .clk(CLK), .clr(RST));
  or or_3 (Lc_0, IDLE_2_q, demultiplexer_3_out1);
  Multiplexer #(.width(32), .enable("false")) multiplexer_3 (
    .in0(c), .in1(c___1_t), .out(multiplexer_3_out), .sel(Write_ASCII));
  Comparator #(.width(32), .mode("unsigned")) comparator_1 (.a({32{1'b0}}), .b(n), .lt(_0_n));  // open: gt, eq
  Comparator #(.width(32), .mode("unsigned")) comparator_2 (.a({32{1'b0}}), .b(c), .lt(_0_c));  // open: gt, eq
  D_Flip_Flop IDLE_3 (.clk(CLK), .D(Write_ASCII), .Q(IDLE_3_q), .reset(RST));  // open: Qn, preset, en
  Demultiplexer #(.enable("false")) demultiplexer_2 (
    .out0(demultiplexer_2_out0), .out1(demultiplexer_2_out1), .in(IDLE_3_q), .sel(_0_c));
  Bit_Extender #(.in_width(32), .out_width(24)) bit_extender_1 (.in(multiplexer_3_out), .out(bit_extender_1_out));
  D_Flip_Flop IDLE_4 (.clk(CLK), .D(Lc_0), .Q(IDLE_4_q), .reset(RST));  // open: Qn, preset, en
  or or_4 (Lc, Lc_0, Write_ASCII);
  or or_5 (Ln, Ln_0, Lc_0);
  Demultiplexer #(.enable("false")) demultiplexer_3 (
    .out0(demultiplexer_3_out0), .out1(demultiplexer_3_out1), .in(IDLE_4_q), .sel(_0_n));
  D_Flip_Flop IDLE_5 (.clk(CLK), .D(demultiplexer_2_out0), .Q(\end ), .reset(RST));  // open: Qn, preset, en
  MEMORY memory_1 (
    .DIR(bit_extender_1_out), .DATA_IN(n___10___48), .WRITE(Lc_0), .CLK(CLK), .CLR(RST),
    .DATA_OUT(memory_1_data_out));
  Bit_Extender #(.in_width(32), .out_width(7)) bit_extender_2 (.in(memory_1_data_out), .out(ASCII));

  // Other names for the same wires on the sheet: Lc_1 = Write_ASCII; Sc = Write_ASCII; Ln_1 = Lc_0; Sn = Lc_0;
  //   Write = Lc_0
endmodule

module PRINT_DEC (
  input  [31:0] num,
  input  start,
  input  CLK,
  input  RST,
  output [6:0] ASCII,
  output Write_ASCII,
  output END
);

  wire demultiplexer_1_out0, demultiplexer_1_out1, demultiplexer_2_out0, demultiplexer_3_out0, end_t,
       IDLE_3_q, IDLE_q, or_1_out, or_2_out, or_3_out, S_ASCII, startUDEC, Write_ASCII_1;
  wire [6:0] ASCII_t;
  wire [31:0] multiplexer_1_out, negator_1_out;

  or or_1 (or_1_out, demultiplexer_1_out0, END);
  Negator #(.width(32)) negator_1 (.in(num), .out(negator_1_out));
  D_Flip_Flop IDLE (.clk(CLK), .D(or_1_out), .Q(IDLE_q), .preset(RST));  // open: Qn, en, reset
  Demultiplexer #(.enable("false")) demultiplexer_1 (
    .out0(demultiplexer_1_out0), .out1(demultiplexer_1_out1), .in(IDLE_q), .sel(start));
  Multiplexer #(.width(32), .enable("false")) multiplexer_1 (
    .in0(num), .in1(negator_1_out), .out(multiplexer_1_out), .sel(num[31]));
  Demultiplexer #(.enable("false")) demultiplexer_2 (
    .out0(demultiplexer_2_out0), .out1(S_ASCII), .in(demultiplexer_1_out1), .sel(num[31]));
  or or_2 (or_2_out, demultiplexer_2_out0, S_ASCII);
  D_Flip_Flop IDLE_2 (.clk(CLK), .D(or_2_out), .Q(startUDEC), .reset(RST));  // open: Qn, preset, en
  PRINT_UDEC print_udec_1 (
    .num(multiplexer_1_out), .start(startUDEC), .CLK(CLK), .RST(RST), .ASCII(ASCII_t),
    .Write_ASCII(Write_ASCII_1), .\end (end_t));
  D_Flip_Flop IDLE_3 (.clk(CLK), .D(or_3_out), .Q(IDLE_3_q), .reset(RST));  // open: Qn, preset, en
  or or_3 (or_3_out, startUDEC, demultiplexer_3_out0);
  Demultiplexer #(.enable("false")) demultiplexer_3 (
    .out0(demultiplexer_3_out0), .out1(END), .in(IDLE_3_q), .sel(end_t));
  Multiplexer #(.width(7), .enable("false")) multiplexer_2 (
    .in0(ASCII_t), .in1(7'b0101101), .out(ASCII), .sel(S_ASCII));
  or or_4 (Write_ASCII, S_ASCII, Write_ASCII_1);

  // Other names for the same wires on the sheet: sign = num[31]; Write_ASCII_0 = S_ASCII
endmodule

module TEST_PRINT (
  input  [31:0] in_1,
  output out_2
);

  wire button_1_out, button_2_out, CLK, CLR, d_ff_1_q, Write_ASCII;
  wire [6:0] ASCII;

  Button button_1 (.out(button_1_out));
  Clock clock_1 (.out(CLK));
  D_Flip_Flop d_ff_1 (.clk(CLK), .D(1'b1), .Q(d_ff_1_q), .reset(button_1_out));  // open: Qn, preset, en
  D_Flip_Flop d_ff_2 (.clk(CLK), .D(d_ff_1_q), .Qn(CLR), .reset(button_1_out));  // open: Q, preset, en
  Button button_2 (.out(button_2_out));
  PRINT_UDEC print_udec_1 ();  // open: num, start, CLK, RST, ASCII, Write_ASCII, end
  PRINT_DEC print_dec_1 (
    .num(in_1), .start(button_2_out), .CLK(CLK), .RST(CLR), .ASCII(ASCII), .Write_ASCII(Write_ASCII),
    .END(out_2));
  TTY #(.rows(32), .cols(60)) tty_1 (.data(ASCII), .clk(CLK), .we(Write_ASCII), .clr(CLR));
endmodule

module Data_path (
  input  [31:0] IOUT,
  input  L_temp,
  input  S_temp,
  input  CLK,
  input  L_a,
  input  L_b,
  input  L_c,
  input  L_d,
  input  L_x,
  input  L_y,
  input  S_x,
  input  S_y,
  input  [1:0] S_Dir,
  input  L_m,
  input  L_n,
  input  CLR,
  output [23:0] DirInput,
  output y__0,
  output [31:0] out_19,
  output [31:0] out_20
);

  wire comparator_1_eq;
  wire [23:0] i, i_1;
  wire [31:0] a, b, c, d, divider_2_out, divider_3_out, divider_4_out, multiplexer_1_out, multiplexer_2_out,
       multiplexer_3_out, multiplier_1_out, multiplier_2_out, multiplier_3_out, subtractor_1_out, temp, x,
       x_y, y;

  Register #(.width(32)) u_a (.D(IOUT), .en(L_a), .Q(a), .clk(CLK), .clr(CLR));
  Multiplexer #(.width(32)) multiplexer_1 (
    .in0({32{1'b0}}), .in1(y), .out(multiplexer_1_out), .sel(S_temp));  // open: en
  Register #(.width(32)) u_Temp (.D(multiplexer_1_out), .en(L_temp), .Q(temp), .clk(CLK), .clr(CLR));
  Register #(.width(32)) u_b (.D(IOUT), .en(L_b), .Q(b), .clk(CLK), .clr(CLR));
  Comparator #(.width(32), .mode("unsigned")) comparator_1 (
    .a(y), .b({32{1'b0}}), .eq(comparator_1_eq));  // open: gt, lt
  not not_1 (y__0, comparator_1_eq);
  Divider #(.width(32)) divider_1 (.a(x), .b(y), .rem(x_y));  // open: out, upper
  Register #(.width(32)) u_c (.D(IOUT), .en(L_c), .Q(c), .clk(CLK), .clr(CLR));
  Multiplexer #(.width(32)) multiplexer_2 (.in0(IOUT), .in1(temp), .out(multiplexer_2_out), .sel(S_x));  // open: en
  Multiplexer #(.width(32)) multiplexer_3 (.in0(IOUT), .in1(x_y), .out(multiplexer_3_out), .sel(S_y));  // open: en
  Divider #(.width(32)) divider_2 (.a(out_19), .b(b), .out(divider_2_out));  // open: upper, rem
  Divider #(.width(32)) divider_3 (.a(out_19), .b(d), .out(divider_3_out));  // open: upper, rem
  Register #(.width(32)) u_d (.D(IOUT), .en(L_d), .Q(d), .clk(CLK), .clr(CLR));
  Register #(.width(32)) u_x (.D(multiplexer_2_out), .en(L_x), .Q(x), .clk(CLK), .clr(CLR));
  Register #(.width(32)) u_y (.D(multiplexer_3_out), .en(L_y), .Q(y), .clk(CLK), .clr(CLR));
  Multiplier #(.width(32)) multiplier_1 (.a(divider_2_out), .b(a), .out(multiplier_1_out));  // open: cin, cout
  Multiplier #(.width(32)) multiplier_2 (.a(divider_3_out), .b(c), .out(multiplier_2_out));  // open: cin, cout
  Adder #(.width(24)) adder_1 (.a(i), .b(24'h1), .out(i_1));  // open: cin, cout
  Subtractor #(.width(32)) subtractor_1 (
    .a(multiplier_1_out), .b(multiplier_2_out), .out(subtractor_1_out));  // open: bin, bout
  Multiplier #(.width(32)) multiplier_3 (.a(b), .b(d), .out(multiplier_3_out));  // open: cin, cout
  Divider #(.width(32)) divider_4 (.a(multiplier_3_out), .b(x), .out(divider_4_out));  // open: upper, rem
  Multiplexer #(.select(2), .width(24)) multiplexer_4 (
    .in0({24{1'b0}}), .in1(24'h1), .in2(24'h2), .in3(24'h3), .out(DirInput), .sel(S_Dir));  // open: en
  Register #(.width(32)) m (.D(divider_4_out), .en(L_m), .Q(out_19), .clk(CLK), .clr(CLR));
  Register #(.width(32)) n (.D(subtractor_1_out), .en(L_n), .Q(out_20), .clk(CLK), .clr(CLR));

  // Other names for the same wires on the sheet: m[31:0] = out_19; n[31:0] = out_20
endmodule

module CU (
  input  reset,
  input  start,
  input  y__0,
  input  clk,
  output S_temp,
  output out_6,
  output L_a,
  output L_b,
  output [1:0] S_Dir,
  output L_c,
  output L_d,
  output L_y,
  output S_x,
  output L_x,
  output S_y,
  output L_temp,
  output L_m,
  output L_n
);

  wire demultiplexer_1_out0, demultiplexer_1_out1, GetC_5_q, GetD_q, IDLE_q, or_6_out, or_7_out, WHILE_q;

  D_Flip_Flop IDLE (.clk(clk), .D(demultiplexer_1_out0), .Q(IDLE_q), .preset(reset));  // open: Qn, en, reset
  Demultiplexer demultiplexer_1 (
    .out0(demultiplexer_1_out0), .out1(demultiplexer_1_out1), .in(IDLE_q), .sel(start));  // open: en
  D_Flip_Flop \wait  (.clk(clk), .D(demultiplexer_1_out1), .Q(L_a), .reset(reset));  // open: Qn, preset, en
  D_Flip_Flop GetA (.clk(clk), .D(L_a), .Q(L_b), .reset(reset));  // open: Qn, preset, en
  or or_1 (S_Dir[0], L_b, L_d);
  or or_2 (S_Dir[1], L_c, L_d);
  or or_3 (L_y, L_d, S_y);
  or or_4 (L_x, L_b, S_x);
  or or_5 (L_temp, L_a, S_temp);
  D_Flip_Flop GetB (.clk(clk), .D(L_b), .Q(L_c), .reset(reset));  // open: Qn, preset, en
  D_Flip_Flop GetC (.clk(clk), .D(L_c), .Q(L_d), .reset(reset));  // open: Qn, preset, en
  D_Flip_Flop GetD (.clk(clk), .D(L_d), .Q(GetD_q), .reset(reset));  // open: Qn, preset, en
  D_Flip_Flop WHILE (.clk(clk), .D(or_6_out), .Q(WHILE_q), .reset(reset));  // open: Qn, preset, en
  Demultiplexer demultiplexer_2 (.out0(L_m), .out1(S_temp), .in(WHILE_q), .sel(y__0));  // open: en
  or or_6 (or_6_out, GetD_q, S_x);
  D_Flip_Flop GetC_2 (.clk(clk), .D(S_temp), .Q(S_y), .reset(reset));  // open: Qn, preset, en
  D_Flip_Flop GetC_3 (.clk(clk), .D(L_m), .Q(L_n), .reset(reset));  // open: Qn, preset, en
  D_Flip_Flop GetC_4 (.clk(clk), .D(S_y), .Q(S_x), .reset(reset));  // open: Qn, preset, en
  or or_7 (or_7_out, L_n, GetC_5_q);
  D_Flip_Flop GetC_5 (.clk(clk), .D(or_7_out), .Q(GetC_5_q), .reset(reset));  // open: Qn, preset, en

  assign out_6 = L_n;

  // Other names for the same wires on the sheet: END = L_n; L_temp0 = L_a; L_temp1 = S_temp; L_x1 = S_x; L_y1 = S_y;
  //   rst = reset; L_x0 = L_b; t_00 = L_b; t_10 = L_c; L_y0 = L_d; t_01 = L_d; t_11 = L_d
endmodule
