// Logisim project BigASM.circ as structural Verilog
module BOARD_BIG_ASM (
  output out_1
);

  wire button_1_out, CLK, CLR, d_ff_1_q, not_1_out, Write, Write_ASCII;
  wire [6:0] ASCII;
  wire [7:0] counter_1_q;
  wire [23:0] Dir_INPUT, Dir_MEMORY;
  wire [31:0] INPUT, MEMORY_IN, MEMORY_OUT;

  Button button_1 (.out(button_1_out));
  Clock clock_1 (.out(CLK));
  D_Flip_Flop d_ff_1 (.clk(CLK), .D(1'b1), .Q(d_ff_1_q), .reset(button_1_out));  // open: Qn, preset, en
  D_Flip_Flop d_ff_2 (.clk(CLK), .D(d_ff_1_q), .Qn(CLR), .reset(button_1_out));  // open: Q, preset, en
  BIG_ASM big_asm_1 (
    .DATA_INPUT(INPUT), .MEMORY_IN(MEMORY_OUT), .CLK(CLK), .CLR(CLR), .DIR_INPUT(Dir_INPUT),
    .MEMORY_OUT(MEMORY_IN), .DIR_MEMORY(Dir_MEMORY), .Write_OUTPUT(Write), .ASCII(ASCII),
    .Write_ASCII(Write_ASCII), .END(out_1));
  MEMORY memory_1 (.DIR(Dir_MEMORY), .DATA_IN(MEMORY_IN), .WRITE(Write), .CLK(CLK), .CLR(CLR), .DATA_OUT(MEMORY_OUT));
  INPUT input_1 (.DIR(Dir_INPUT), .CLK(CLK), .DATA_OUT(INPUT));
  Counter counter_1 (.load(1'b0), .count(not_1_out), .Q(counter_1_q), .clk(CLK), .clr(CLR));  // open: D, carry
  not not_1 (not_1_out, out_1);
  // Probe on counter_1_q
  TTY #(.rows(32), .cols(60)) tty_1 (.data(ASCII), .clk(CLK), .we(Write_ASCII), .clr(CLR));

  // Other names for the same wires on the sheet: END = out_1

  // Notes on the sheet:
  //   COUNTER
  //   BOARD
endmodule

module INPUT (
  input  [23:0] DIR,
  input  CLK,
  output [31:0] DATA_OUT
);

  RAM #(.addrWidth(24), .dataWidth(32)) ram_1 (.addr(DIR), .data(DATA_OUT), .clk(CLK), .ld(1'b1));  // open: sel, clr
endmodule

module MEMORY (
  input  [23:0] DIR,
  input  [31:0] DATA_IN,
  input  WRITE,
  input  CLK,
  input  CLR,
  output [31:0] DATA_OUT
);

  wire not_1_out;

  not not_1 (not_1_out, WRITE);
  RAM #(.addrWidth(24), .dataWidth(32), .bus("separate")) ram_1 (
    .addr(DIR), .din(DATA_IN), .data(DATA_OUT), .clk(CLK), .ld(not_1_out), .clr(CLR));  // open: str, sel
endmodule

module BIG_ASM (
  input  [31:0] DATA_INPUT,
  input  [31:0] MEMORY_IN,
  input  CLK,
  input  CLR,
  output [23:0] DIR_INPUT,
  output [31:0] MEMORY_OUT,
  output [23:0] DIR_MEMORY,
  output Write_OUTPUT,
  output [6:0] ASCII,
  output Write_ASCII,
  output END
);

  wire cu_1_l_a, cu_1_l_i, cu_1_l_k, cu_1_l_m, cu_1_l_n, cu_1_s_i, cu_1_s_k, cu_1_s_m, data_path_1_i__n_1,
       end0, GetB_q, or_1_out;
  wire [1:0] cu_1_s_dir;
  wire [31:0] data_path_1_out_14;

  CU cu_1 (
    .reset(CLR), .start(1'b1), .clk(CLK), .i__n_1(data_path_1_i__n_1), .L_a(cu_1_l_a), .L_n(cu_1_l_n),
    .S_i(cu_1_s_i), .L_i(cu_1_l_i), .S_Dir(cu_1_s_dir), .S_m(cu_1_s_m), .L_m(cu_1_l_m), .S_k(cu_1_s_k),
    .L_k(cu_1_l_k), .out_5(end0));
  Data_Path data_path_1 (
    .IOUT(DATA_INPUT), .CLR(CLR), .CLK(CLK), .L_a(cu_1_l_a), .L_n(cu_1_l_n), .S_i(cu_1_s_i), .L_i(cu_1_l_i),
    .S_Dir(cu_1_s_dir), .S_m(cu_1_s_m), .L_m(cu_1_l_m), .S_k(cu_1_s_k), .L_k(cu_1_l_k), .DirInput(DIR_INPUT),
    .out_14(data_path_1_out_14), .i__n_1(data_path_1_i__n_1));
  // Probe on data_path_1_out_14
  PRINT_DEC print_dec_1 (
    .num(data_path_1_out_14), .start(end0), .CLK(CLK), .RST(CLR), .ASCII(ASCII), .Write_ASCII(Write_ASCII),
    .END(END));
  or or_1 (or_1_out, END, GetB_q);
  D_Flip_Flop GetB (.clk(CLK), .D(or_1_out), .Q(GetB_q), .reset(CLR));  // open: Qn, preset, en

  // Other names for the same wires on the sheet: rst = CLR
endmodule

module PRINT_UDEC (
  input  [31:0] num,
  input  start,
  input  CLK,
  input  RST,
  output [6:0] ASCII,
  output Write_ASCII,
  output \end 
);

  wire _0_c, _0_n, demultiplexer_1_out0, demultiplexer_2_out0, demultiplexer_2_out1, demultiplexer_3_out0,
       demultiplexer_3_out1, IDLE_2_q, IDLE_3_q, IDLE_4_q, IDLE_q, Lc, Lc_0, Ln, Ln_0, or_1_out;
  wire [23:0] bit_extender_1_out;
  wire [31:0] c, c___1, c___1_t, divider_1_rem, memory_1_data_out, multiplexer_1_out, multiplexer_2_out,
       multiplexer_3_out, n, n___10, n___10___48;

  Multiplexer #(.width(32), .enable("false")) multiplexer_1 (
    .in0(num), .in1(n___10), .out(multiplexer_1_out), .sel(Lc_0));
  Divider #(.width(32)) divider_1 (.a(n), .b(32'ha), .out(n___10), .rem(divider_1_rem));  // open: upper
  Adder #(.width(32)) adder_1 (.a(divider_1_rem), .b(32'h30), .out(n___10___48));  // open: cin, cout
  or or_1 (or_1_out, demultiplexer_1_out0, \end );
  Register #(.width(32)) u_n (.D(multiplexer_1_out), .en(Ln), .Q(n), .clk(CLK), .clr(RST));
  D_Flip_Flop IDLE (.clk(CLK), .D(or_1_out), .Q(IDLE_q), .preset(RST));  // open: Qn, en, reset
  Demultiplexer #(.enable("false")) demultiplexer_1 (
    .out0(demultiplexer_1_out0), .out1(Ln_0), .in(IDLE_q), .sel(start));
  or or_2 (Write_ASCII, demultiplexer_3_out0, demultiplexer_2_out1);
  Multiplexer #(.width(32), .enable("false")) multiplexer_2 (
    .in0(c___1), .in1(c___1_t), .out(multiplexer_2_out), .sel(Write_ASCII));
  Adder #(.width(32)) adder_2 (.a(c), .b(32'h1), .out(c___1));  // open: cin, cout
  Subtractor #(.width(32)) subtractor_1 (.a(c), .b(32'h1), .out(c___1_t));  // open: bin, bout
  D_Flip_Flop IDLE_2 (.clk(CLK), .D(Ln_0), .Q(IDLE_2_q), .reset(RST));  // open: Qn, preset, en
  Register #(.width(32)) u_c (.D(multiplexer_2_out), .en(Lc), .Q(c), .clk(CLK), .clr(RST));
  or or_3 (Lc_0, IDLE_2_q, demultiplexer_3_out1);
  Multiplexer #(.width(32), .enable("false")) multiplexer_3 (
    .in0(c), .in1(c___1_t), .out(multiplexer_3_out), .sel(Write_ASCII));
  Comparator #(.width(32), .mode("unsigned")) comparator_1 (.a({32{1'b0}}), .b(n), .lt(_0_n));  // open: gt, eq
  Comparator #(.width(32), .mode("unsigned")) comparator_2 (.a({32{1'b0}}), .b(c), .lt(_0_c));  // open: gt, eq
  D_Flip_Flop IDLE_3 (.clk(CLK), .D(Write_ASCII), .Q(IDLE_3_q), .reset(RST));  // open: Qn, preset, en
  Demultiplexer #(.enable("false")) demultiplexer_2 (
    .out0(demultiplexer_2_out0), .out1(demultiplexer_2_out1), .in(IDLE_3_q), .sel(_0_c));
  Bit_Extender #(.in_width(32), .out_width(24)) bit_extender_1 (.in(multiplexer_3_out), .out(bit_extender_1_out));
  D_Flip_Flop IDLE_4 (.clk(CLK), .D(Lc_0), .Q(IDLE_4_q), .reset(RST));  // open: Qn, preset, en
  or or_4 (Lc, Lc_0, Write_ASCII);
  or or_5 (Ln, Ln_0, Lc_0);
  Demultiplexer #(.enable("false")) demultiplexer_3 (
    .out0(demultiplexer_3_out0), .out1(demultiplexer_3_out1), .in(IDLE_4_q), .sel(_0_n));
  D_Flip_Flop IDLE_5 (.clk(CLK), .D(demultiplexer_2_out0), .Q(\end ), .reset(RST));  // open: Qn, preset, en
  MEMORY memory_1 (
    .DIR(bit_extender_1_out), .DATA_IN(n___10___48), .WRITE(Lc_0), .CLK(CLK), .CLR(RST),
    .DATA_OUT(memory_1_data_out));
  Bit_Extender #(.in_width(32), .out_width(7)) bit_extender_2 (.in(memory_1_data_out), .out(ASCII));

  // Other names for the same wires on the sheet: Lc_1 = Write_ASCII; Sc = Write_ASCII; Ln_1 = Lc_0; Sn = Lc_0;
  //   Write = Lc_0
endmodule

module PRINT_DEC (
  input  [31:0] num,
  input  start,
  input  CLK,
  input  RST,
  output [6:0] ASCII,
  output Write_ASCII,
  output END
);

  wire demultiplexer_1_out0, demultiplexer_1_out1, demultiplexer_2_out0, demultiplexer_3_out0, end_t,
       IDLE_3_q, IDLE_q, or_1_out, or_2_out, or_3_out, S_ASCII, startUDEC, Write_ASCII_1;
  wire [6:0] ASCII_t;
  wire [31:0] multiplexer_1_out, negator_1_out;

  or or_1 (or_1_out, demultiplexer_1_out0, END);
  Negator #(.width(32)) negator_1 (.in(num), .out(negator_1_out));
  D_Flip_Flop IDLE (.clk(CLK), .D(or_1_out), .Q(IDLE_q), .preset(RST));  // open: Qn, en, reset
  Demultiplexer #(.enable("false")) demultiplexer_1 (
    .out0(demultiplexer_1_out0), .out1(demultiplexer_1_out1), .in(IDLE_q), .sel(start));
  Multiplexer #(.width(32), .enable("false")) multiplexer_1 (
    .in0(num), .in1(negator_1_out), .out(multiplexer_1_out), .sel(num[31]));
  Demultiplexer #(.enable("false")) demultiplexer_2 (
    .out0(demultiplexer_2_out0), .out1(S_ASCII), .in(demultiplexer_1_out1), .sel(num[31]));
  or or_2 (or_2_out, demultiplexer_2_out0, S_ASCII);
  D_Flip_Flop IDLE_2 (.clk(CLK), .D(or_2_out), .Q(startUDEC), .reset(RST));  // open: Qn, preset, en
  PRINT_UDEC print_udec_1 (
    .num(multiplexer_1_out), .start(startUDEC), .CLK(CLK), .RST(RST), .ASCII(ASCII_t),
    .Write_ASCII(Write_ASCII_1), .\end (end_t));
  D_Flip_Flop IDLE_3 (.clk(CLK), .D(or_3_out), .Q(IDLE_3_q), .reset(RST));  // open: Qn, preset, en
  or or_3 (or_3_out, startUDEC, demultiplexer_3_out0);
  Demultiplexer #(.enable("false")) demultiplexer_3 (
    .out0(demultiplexer_3_out0), .out1(END), .in(IDLE_3_q), .sel(end_t));
  Multiplexer #(.width(7), .enable("false")) multiplexer_2 (
    .in0(ASCII_t), .in1(7'b0101101), .out(ASCII), .sel(S_ASCII));
  or or_4 (Write_ASCII, S_ASCII, Write_ASCII_1);

  // Other names for the same wires on the sheet: sign = num[31]; Write_ASCII_0 = S_ASCII
endmodule

module TEST_PRINT (
  input  [31:0] in_1,
  output out_2
);

  wire button_1_out, button_2_out, CLK, CLR, d_ff_1_q, Write_ASCII;
  wire [6:0] ASCII;

  Button button_1 (.out(button_1_out));
  Clock clock_1 (.out(CLK));
  D_Flip_Flop d_ff_1 (.clk(CLK), .D(1'b1), .Q(d_ff_1_q), .reset(button_1_out));  // open: Qn, preset, en
  D_Flip_Flop d_ff_2 (.clk(CLK), .D(d_ff_1_q), .Qn(CLR), .reset(button_1_out));  // open: Q, preset, en
  Button button_2 (.out(button_2_out));
  PRINT_UDEC print_udec_1 ();  // open: num, start, CLK, RST, ASCII, Write_ASCII, end
  PRINT_DEC print_dec_1 (
    .num(in_1), .start(button_2_out), .CLK(CLK), .RST(CLR), .ASCII(ASCII), .Write_ASCII(Write_ASCII),
    .END(out_2));
  TTY #(.rows(32), .cols(60)) tty_1 (.data(ASCII), .clk(CLK), .we(Write_ASCII), .clr(CLR));
endmodule

module Data_Path (
  input  [31:0] IOUT,
  input  CLR,
  input  CLK,
  input  L_a,
  input  L_n,
  input  S_i,
  input  L_i,
  input  [1:0] S_Dir,
  input  S_m,
  input  L_m,
  input  S_k,
  input  L_k,
  output [23:0] DirInput,
  output [31:0] out_14,
  output i__n_1
);

  wire comparator_1_gt;
  wire [23:0] i, i_1, i_2, multiplexer_1_out, undriven;
  wire [31:0] a, bit_extender_1_out, k, k_a, m_star, multiplexer_2_out, multiplexer_3_out, multiplier_2_out,
       n, n_1;

  Register #(.width(32)) u_a (.D(IOUT), .en(L_a), .Q(a), .clk(CLK), .clr(CLR));
  Multiplexer #(.width(24)) multiplexer_1 (.in0(24'h2), .in1(i_1), .out(multiplexer_1_out), .sel(S_i));  // open: en
  Multiplier #(.width(32)) multiplier_1 (.a(k), .b(a), .out(k_a));  // open: cin, cout
  Register #(.width(32)) u_n (.D(IOUT), .en(L_n), .Q(n), .clk(CLK), .clr(CLR));
  Register #(.width(24)) u_i (.D(multiplexer_1_out), .en(L_i), .Q(i), .clk(CLK), .clr(CLR));
  Adder #(.width(24)) adder_1 (.a(i), .b(24'h1), .out(i_1));  // open: cin, cout
  Adder #(.width(32)) adder_2 (.a(n), .b(32'h1), .out(n_1));  // open: cin, cout
  Multiplexer #(.width(32)) multiplexer_2 (
    .in0({32{1'b0}}), .in1(m_star), .out(multiplexer_2_out), .sel(S_m));  // open: en
  Multiplexer #(.width(32)) multiplexer_3 (.in0(32'h1), .in1(k_a), .out(multiplexer_3_out), .sel(S_k));  // open: en
  Subtractor #(.width(24)) subtractor_1 (.a(i), .b(24'h2), .out(i_2));  // open: bin, bout
  Multiplier #(.width(32)) multiplier_2 (.a(k), .b(IOUT), .out(multiplier_2_out));  // open: cin, cout
  Register #(.width(32)) m (.D(multiplexer_2_out), .en(L_m), .Q(out_14), .clk(CLK), .clr(CLR));
  Register #(.width(32)) u_k (.D(multiplexer_3_out), .en(L_k), .Q(k), .clk(CLK), .clr(CLR));
  assign bit_extender_1_out = {{8{1'b0}}, i};  // Bit_Extender bit_extender_1
  Adder #(.width(32)) adder_3 (.a(out_14), .b(multiplier_2_out), .out(m_star));  // open: cin, cout
  not not_1 (i__n_1, comparator_1_gt);
  Comparator #(.width(32), .mode("unsigned")) comparator_1 (
    .a(bit_extender_1_out), .b(n_1), .gt(comparator_1_gt));  // open: eq, lt
  // Probe on out_14
  Multiplexer #(.select(2), .width(24)) multiplexer_4 (
    .in0({24{1'b0}}), .in1(24'h1), .in2(i), .in3(undriven), .out(DirInput), .sel(S_Dir));  // open: en

  // Other names for the same wires on the sheet: m[31:0] = out_14
endmodule

module CU (
  input  reset,
  input  start,
  input  clk,
  input  i__n_1,
  output out_5,
  output L_a,
  output L_n,
  output S_i,
  output L_i,
  output [1:0] S_Dir,
  output S_m,
  output L_m,
  output S_k,
  output L_k
);

  wire demultiplexer_1_out0, demultiplexer_1_out1, GetB_2_q, GetC_q, IDLE_q, or_4_out, or_5_out, while_q;

  or or_1 (L_i, L_a, S_i);
  or or_2 (L_m, L_a, S_Dir[1]);
  or or_3 (L_k, L_a, S_i);
  D_Flip_Flop IDLE (.clk(clk), .D(demultiplexer_1_out0), .Q(IDLE_q), .preset(reset));  // open: Qn, en, reset
  Demultiplexer demultiplexer_1 (
    .out0(demultiplexer_1_out0), .out1(demultiplexer_1_out1), .in(IDLE_q), .sel(start));  // open: en
  D_Flip_Flop GetB (.clk(clk), .reset(reset));  // open: D, Q, Qn, preset, en
  D_Flip_Flop \wait  (.clk(clk), .D(demultiplexer_1_out1), .Q(L_a), .reset(reset));  // open: Qn, preset, en
  D_Flip_Flop GetA (.clk(clk), .D(L_a), .Q(L_n), .reset(reset));  // open: Qn, preset, en
  D_Flip_Flop GetB_2 (.clk(clk), .D(L_n), .Q(GetB_2_q), .reset(reset));  // open: Qn, preset, en
  or or_4 (or_4_out, GetB_2_q, S_i);
  Demultiplexer demultiplexer_2 (.out0(out_5), .out1(S_Dir[1]), .in(while_q), .sel(i__n_1));  // open: en
  D_Flip_Flop \while  (.clk(clk), .D(or_4_out), .Q(while_q), .reset(reset));  // open: Qn, preset, en
  D_Flip_Flop GetB_3 (.clk(clk), .D(S_Dir[1]), .Q(S_i), .reset(reset));  // open: Qn, preset, en
  or or_5 (or_5_out, out_5, GetC_q);
  D_Flip_Flop GetC (.clk(clk), .D(or_5_out), .Q(GetC_q), .reset(reset));  // open: Qn, preset, en

  assign S_Dir[0] = L_n;
  assign S_k = S_i;
  assign S_m = S_Dir[1];

  // Other names for the same wires on the sheet: END = out_5; L_i1 = S_i; L_k1 = S_i; L_i0 = L_a; L_k0 = L_a;
  //   L_m0 = L_a; rst = reset; S_Dir0 = L_n; L_m1 = S_Dir[1]
endmodule
