// Logisim project BigASM.circ as structural Verilog
module BOARD_BIG_ASM (
  output out_1
);

  wire button_1_out, CLK, CLR, d_ff_1_q, not_1_out, Write, Write_ASCII;
  wire [6:0] ASCII;
  wire [7:0] counter_1_q;
  wire [23:0] Dir_INPUT, Dir_MEMORY;
  wire [31:0] INPUT, MEMORY_IN, MEMORY_OUT;

  Button button_1 (.out(button_1_out));
  Clock clock_1 (.out(CLK));
  D_Flip_Flop d_ff_1 (.clk(CLK), .D(1'b1), .Q(d_ff_1_q), .reset(button_1_out));  // open: Qn, preset, en
  D_Flip_Flop d_ff_2 (.clk(CLK), .D(d_ff_1_q), .Qn(CLR), .reset(button_1_out));  // open: Q, preset, en
  BIG_ASM big_asm_1 (
    .DATA_INPUT(INPUT), .MEMORY_IN(MEMORY_OUT), .CLK(CLK), .CLR(CLR), .DIR_INPUT(Dir_INPUT),
    .MEMORY_OUT(MEMORY_IN), .DIR_MEMORY(Dir_MEMORY), .Write_OUTPUT(Write), .ASCII(ASCII),
    .Write_ASCII(Write_ASCII), .END(out_1));  // open: Output, END_2
  MEMORY memory_1 (.DIR(Dir_MEMORY), .DATA_IN(MEMORY_IN), .WRITE(Write), .CLK(CLK), .CLR(CLR), .DATA_OUT(MEMORY_OUT));
  // Probe on INPUT
  INPUT input_1 (.DIR(Dir_INPUT), .CLK(CLK), .DATA_OUT(INPUT));
  Counter counter_1 (.load(1'b0), .count(not_1_out), .Q(counter_1_q), .clk(CLK), .clr(CLR));  // open: D, carry
  not not_1 (not_1_out, out_1);
  // Probe on ASCII
  // Probe on counter_1_q
  TTY #(.rows(32), .cols(60)) tty_1 (.data(ASCII), .clk(CLK), .we(Write_ASCII), .clr(CLR));

  // Other names for the same wires on the sheet: END = out_1

  // Notes on the sheet:
  //   COUNTER
  //   BOARD
endmodule

module INPUT (
  input  [23:0] DIR,
  input  CLK,
  output [31:0] DATA_OUT
);

  RAM #(.addrWidth(24), .dataWidth(32)) ram_1 (.addr(DIR), .data(DATA_OUT), .clk(CLK), .ld(1'b1));  // open: sel, clr
endmodule

module MEMORY (
  input  [23:0] DIR,
  input  [31:0] DATA_IN,
  input  WRITE,
  input  CLK,
  input  CLR,
  output [31:0] DATA_OUT
);

  wire not_1_out;

  not not_1 (not_1_out, WRITE);
  RAM #(.addrWidth(24), .dataWidth(32), .bus("separate")) ram_1 (
    .addr(DIR), .din(DATA_IN), .data(DATA_OUT), .clk(CLK), .ld(not_1_out), .clr(CLR));  // open: str, sel
endmodule

module BIG_ASM (
  input  [31:0] DATA_INPUT,
  input  [31:0] MEMORY_IN,
  input  CLK,
  input  CLR,
  output [23:0] DIR_INPUT,
  output [31:0] MEMORY_OUT,
  output [23:0] DIR_MEMORY,
  output Write_OUTPUT,
  output [6:0] ASCII,
  output Write_ASCII,
  output END,
  output Output,
  output END_2
);

  wire a___0, a___b, b___0, C, C1, div_cu_1_la, div_cu_1_lb, div_cu_1_sa, not_1_out, not_2_out, not_3_out,
       select, Start2;
  wire [31:0] A, B, counter_1_q, demultiplexer_1_out0, demultiplexer_1_out1;

  Counter #(.width(32), .max('hffffffff)) counter_1 (
    .load(1'b0), .D({32{1'b0}}), .Q(counter_1_q), .clk(CLK), .clr(CLR));  // open: count, carry
  BitSelector #(.width(32)) bitselector_1 (.in(counter_1_q), .out(select), .sel({5{1'b0}}));
  Comparator #(.width(32), .mode("unsigned")) comparator_1 (.a(counter_1_q), .b(32'h2), .gt(Start2));  // open: eq, lt
  Demultiplexer #(.width(32)) demultiplexer_1 (
    .out0(demultiplexer_1_out0), .out1(demultiplexer_1_out1), .in(DATA_INPUT), .sel(select));  // open: en
  not not_1 (not_1_out, Start2);
  not not_2 (not_2_out, select);
  not not_3 (not_3_out, Start2);
  and and_1 (C1, not_1_out, not_2_out);
  and and_2 (C, not_3_out, select);
  Register #(.width(32), .trigger("falling")) register_1 (
    .D(demultiplexer_1_out0), .en(C1), .Q(A), .clk(CLK), .clr(CLR));
  Register #(.width(32)) register_2 (.D(demultiplexer_1_out1), .en(C), .Q(B), .clk(CLK), .clr(CLR));
  // Probe on A
  // Probe on B
  // Probe on demultiplexer_1_out0
  Div_CU div_cu_1 (
    .a___0(a___0), .a___b(a___b), .b___0(b___0), .reset(CLR), .start(Start2), .clk(CLK), .Output(Output),
    .END(END), .Sa(div_cu_1_sa), .La(div_cu_1_la), .Lb(div_cu_1_lb));
  // Probe on demultiplexer_1_out1
  Multiplexer #(.width(24)) multiplexer_1 (.in0({24{1'b0}}), .in1(24'h1), .out(DIR_INPUT), .sel(select));  // open: en
  Div_DataP div_datap_1 (
    .Ain(A), .Bin(B), .Sa(div_cu_1_sa), .La(div_cu_1_la), .Lb(div_cu_1_lb), .A___0(a___0), .A___B(a___b),
    .B___0(b___0), .CLK(CLK));
  // Probe on DIR_INPUT
  assign ASCII = {{6{1'b0}}, Output};  // Bit_Extender bit_extender_1

  assign END_2 = END;
  assign Write_ASCII = END;
  assign Write_OUTPUT = END;

  // Other names for the same wires on the sheet: rst = CLR
endmodule

module PRINT_UDEC (
  input  [31:0] num,
  input  start,
  input  CLK,
  input  RST,
  output [6:0] ASCII,
  output Write_ASCII,
  output \end 
);

  wire _0_c, _0_n, demultiplexer_1_out0, demultiplexer_2_out0, demultiplexer_2_out1, demultiplexer_3_out0,
       demultiplexer_3_out1, IDLE_2_q, IDLE_3_q, IDLE_4_q, IDLE_q, Lc, Lc_0, Ln, Ln_0, or_1_out;
  wire [23:0] bit_extender_1_out;
  wire [31:0] c, c___1, c___1_t, divider_1_rem, memory_1_data_out, multiplexer_1_out, multiplexer_2_out,
       multiplexer_3_out, n, n___10, n___10___48;

  Multiplexer #(.width(32), .enable("false")) multiplexer_1 (
    .in0(num), .in1(n___10), .out(multiplexer_1_out), .sel(Lc_0));
  Divider #(.width(32)) divider_1 (.a(n), .b(32'ha), .out(n___10), .rem(divider_1_rem));  // open: upper
  Adder #(.width(32)) adder_1 (.a(divider_1_rem), .b(32'h30), .out(n___10___48));  // open: cin, cout
  or or_1 (or_1_out, demultiplexer_1_out0, \end );
  Register #(.width(32)) u_n (.D(multiplexer_1_out), .en(Ln), .Q(n), .clk(CLK), .clr(RST));
  D_Flip_Flop IDLE (.clk(CLK), .D(or_1_out), .Q(IDLE_q), .preset(RST));  // open: Qn, en, reset
  Demultiplexer #(.enable("false")) demultiplexer_1 (
    .out0(demultiplexer_1_out0), .out1(Ln_0), .in(IDLE_q), .sel(start));
  or or_2 (Write_ASCII, demultiplexer_3_out0, demultiplexer_2_out1);
  Multiplexer #(.width(32), .enable("false")) multiplexer_2 (
    .in0(c___1), .in1(c___1_t), .out(multiplexer_2_out), .sel(Write_ASCII));
  Adder #(.width(32)) adder_2 (.a(c), .b(32'h1), .out(c___1));  // open: cin, cout
  Subtractor #(.width(32)) subtractor_1 (.a(c), .b(32'h1), .out(c___1_t));  // open: bin, bout
  D_Flip_Flop IDLE_2 (.clk(CLK), .D(Ln_0), .Q(IDLE_2_q), .reset(RST));  // open: Qn, preset, en
  Register #(.width(32)) u_c (.D(multiplexer_2_out), .en(Lc), .Q(c), .clk(CLK), .clr(RST));
  or or_3 (Lc_0, IDLE_2_q, demultiplexer_3_out1);
  Multiplexer #(.width(32), .enable("false")) multiplexer_3 (
    .in0(c), .in1(c___1_t), .out(multiplexer_3_out), .sel(Write_ASCII));
  Comparator #(.width(32), .mode("unsigned")) comparator_1 (.a({32{1'b0}}), .b(n), .lt(_0_n));  // open: gt, eq
  Comparator #(.width(32), .mode("unsigned")) comparator_2 (.a({32{1'b0}}), .b(c), .lt(_0_c));  // open: gt, eq
  D_Flip_Flop IDLE_3 (.clk(CLK), .D(Write_ASCII), .Q(IDLE_3_q), .reset(RST));  // open: Qn, preset, en
  Demultiplexer #(.enable("false")) demultiplexer_2 (
    .out0(demultiplexer_2_out0), .out1(demultiplexer_2_out1), .in(IDLE_3_q), .sel(_0_c));
  Bit_Extender #(.in_width(32), .out_width(24)) bit_extender_1 (.in(multiplexer_3_out), .out(bit_extender_1_out));
  D_Flip_Flop IDLE_4 (.clk(CLK), .D(Lc_0), .Q(IDLE_4_q), .reset(RST));  // open: Qn, preset, en
  or or_4 (Lc, Lc_0, Write_ASCII);
  or or_5 (Ln, Ln_0, Lc_0);
  Demultiplexer #(.enable("false")) demultiplexer_3 (
    .out0(demultiplexer_3_out0), .out1(demultiplexer_3_out1), .in(IDLE_4_q), .sel(_0_n));
  D_Flip_Flop IDLE_5 (.clk(CLK), .D(demultiplexer_2_out0), .Q(\end ), .reset(RST));  // open: Qn, preset, en
  MEMORY memory_1 (
    .DIR(bit_extender_1_out), .DATA_IN(n___10___48), .WRITE(Lc_0), .CLK(CLK), .CLR(RST),
    .DATA_OUT(memory_1_data_out));
  Bit_Extender #(.in_width(32), .out_width(7)) bit_extender_2 (.in(memory_1_data_out), .out(ASCII));

  // Other names for the same wires on the sheet: Lc_1 = Write_ASCII; Sc = Write_ASCII; Ln_1 = Lc_0; Sn = Lc_0;
  //   Write = Lc_0
endmodule

module PRINT_DEC (
  input  [31:0] num,
  input  start,
  input  CLK,
  input  RST,
  output [6:0] ASCII,
  output Write_ASCII,
  output END
);

  wire demultiplexer_1_out0, demultiplexer_1_out1, demultiplexer_2_out0, demultiplexer_3_out0, end_t,
       IDLE_3_q, IDLE_q, or_1_out, or_2_out, or_3_out, S_ASCII, startUDEC, Write_ASCII_1;
  wire [6:0] ASCII_t;
  wire [31:0] multiplexer_1_out, negator_1_out;

  or or_1 (or_1_out, demultiplexer_1_out0, END);
  Negator #(.width(32)) negator_1 (.in(num), .out(negator_1_out));
  D_Flip_Flop IDLE (.clk(CLK), .D(or_1_out), .Q(IDLE_q), .preset(RST));  // open: Qn, en, reset
  Demultiplexer #(.enable("false")) demultiplexer_1 (
    .out0(demultiplexer_1_out0), .out1(demultiplexer_1_out1), .in(IDLE_q), .sel(start));
  Multiplexer #(.width(32), .enable("false")) multiplexer_1 (
    .in0(num), .in1(negator_1_out), .out(multiplexer_1_out), .sel(num[31]));
  Demultiplexer #(.enable("false")) demultiplexer_2 (
    .out0(demultiplexer_2_out0), .out1(S_ASCII), .in(demultiplexer_1_out1), .sel(num[31]));
  or or_2 (or_2_out, demultiplexer_2_out0, S_ASCII);
  D_Flip_Flop IDLE_2 (.clk(CLK), .D(or_2_out), .Q(startUDEC), .reset(RST));  // open: Qn, preset, en
  PRINT_UDEC print_udec_1 (
    .num(multiplexer_1_out), .start(startUDEC), .CLK(CLK), .RST(RST), .ASCII(ASCII_t),
    .Write_ASCII(Write_ASCII_1), .\end (end_t));
  D_Flip_Flop IDLE_3 (.clk(CLK), .D(or_3_out), .Q(IDLE_3_q), .reset(RST));  // open: Qn, preset, en
  or or_3 (or_3_out, startUDEC, demultiplexer_3_out0);
  Demultiplexer #(.enable("false")) demultiplexer_3 (
    .out0(demultiplexer_3_out0), .out1(END), .in(IDLE_3_q), .sel(end_t));
  Multiplexer #(.width(7), .enable("false")) multiplexer_2 (
    .in0(ASCII_t), .in1(7'b0101101), .out(ASCII), .sel(S_ASCII));
  or or_4 (Write_ASCII, S_ASCII, Write_ASCII_1);

  // Other names for the same wires on the sheet: sign = num[31]; Write_ASCII_0 = S_ASCII
endmodule

module TEST_PRINT (
  input  [31:0] in_1,
  output out_2
);

  wire button_1_out, button_2_out, CLK, CLR, d_ff_1_q, Write_ASCII;
  wire [6:0] ASCII;

  Button button_1 (.out(button_1_out));
  Clock clock_1 (.out(CLK));
  D_Flip_Flop d_ff_1 (.clk(CLK), .D(1'b1), .Q(d_ff_1_q), .reset(button_1_out));  // open: Qn, preset, en
  D_Flip_Flop d_ff_2 (.clk(CLK), .D(d_ff_1_q), .Qn(CLR), .reset(button_1_out));  // open: Q, preset, en
  Button button_2 (.out(button_2_out));
  PRINT_UDEC print_udec_1 ();  // open: num, start, CLK, RST, ASCII, Write_ASCII, end
  PRINT_DEC print_dec_1 (
    .num(in_1), .start(button_2_out), .CLK(CLK), .RST(CLR), .ASCII(ASCII), .Write_ASCII(Write_ASCII),
    .END(out_2));
  // Probe on ASCII
  TTY #(.rows(32), .cols(60)) tty_1 (.data(ASCII), .clk(CLK), .we(Write_ASCII), .clr(CLR));
endmodule

module Div_DataP (
  input  [31:0] Ain,
  input  [31:0] Bin,
  input  Sa,
  input  La,
  input  Lb,
  input  CLK,
  output A___0,
  output A___B,
  output B___0
);

  wire [31:0] A, A_B, B, multiplexer_1_out;

  Multiplexer #(.width(32)) multiplexer_1 (.in0(Ain), .in1(A_B), .out(multiplexer_1_out), .sel(Sa));  // open: en
  Register #(.width(32)) u_A (.D(multiplexer_1_out), .en(La), .Q(A), .clk(CLK));  // open: clr
  Register #(.width(32)) u_B (.D(Bin), .en(Lb), .Q(B), .clk(CLK));  // open: clr
  Comparator #(.width(32), .mode("unsigned")) comparator_1 (.a(A), .b(B), .lt(A___B));  // open: gt, eq
  Subtractor #(.width(32)) subtractor_1 (.a(A), .b(B), .out(A_B));  // open: bin, bout
  nor nor_1 (A___0, A[0], A[1], A[2], A[3], A[4], A[5], A[6], A[7], A[8], A[9], A[10], A[11], A[12], A[13], A[14], A[15], A[16], A[17], A[18], A[19], A[20], A[21], A[22], A[23], A[24], A[25], A[26], A[27], A[28], A[29], A[30], A[31]);
  nor nor_2 (B___0, B[0], B[1], B[2], B[3], B[4], B[5], B[6], B[7], B[8], B[9], B[10], B[11], B[12], B[13], B[14], B[15], B[16], B[17], B[18], B[19], B[20], B[21], B[22], B[23], B[24], B[25], B[26], B[27], B[28], B[29], B[30], B[31]);
endmodule

module Div_CU (
  input  a___0,
  input  a___b,
  input  b___0,
  input  reset,
  input  start,
  input  clk,
  output Output,
  output END,
  output Sa,
  output La,
  output Lb
);

  wire demultiplexer_1_out0, demultiplexer_2_out0, demultiplexer_3_out0, demultiplexer_4_out0,
       demultiplexer_5_out0, demultiplexer_6_out0, demultiplexer_7_out0, demultiplexer_8_out0, END1, F1, F2,
       F3, Fisrt_Comps_q, IDLE_q, or_1_out, or_2_out, or_3_out, or_4_out, restart1, restart2, T1, T2;

  or or_1 (or_1_out, demultiplexer_3_out0, restart1, restart2);
  Demultiplexer demultiplexer_1 (.out0(demultiplexer_1_out0), .out1(T2), .in(Sa), .sel(a___0));  // open: en
  D_Flip_Flop IDLE (.clk(clk), .D(or_1_out), .Q(IDLE_q), .preset(reset));  // open: Qn, en, reset
  Demultiplexer demultiplexer_2 (
    .out0(demultiplexer_2_out0), .out1(F3), .in(demultiplexer_1_out0), .sel(a___b));  // open: en
  Demultiplexer demultiplexer_3 (.out0(demultiplexer_3_out0), .out1(Lb), .in(IDLE_q), .sel(start));  // open: en
  or or_2 (or_2_out, F1, demultiplexer_4_out0, F2, F3);
  Demultiplexer demultiplexer_4 (.out0(demultiplexer_4_out0), .out1(restart1), .in(END1), .sel(start));  // open: en
  D_Flip_Flop FALSE (.clk(clk), .D(or_2_out), .Q(END1), .reset(reset));  // open: Qn, preset, en
  Demultiplexer demultiplexer_5 (.out0(demultiplexer_5_out0), .out1(F1), .in(Fisrt_Comps_q), .sel(b___0));  // open: en
  D_Flip_Flop Fisrt_Comps (.clk(clk), .D(Lb), .Q(Fisrt_Comps_q), .reset(reset));  // open: Qn, preset, en
  Demultiplexer demultiplexer_6 (
    .out0(demultiplexer_6_out0), .out1(T1), .in(demultiplexer_5_out0), .sel(a___0));  // open: en
  or or_3 (or_3_out, demultiplexer_8_out0, T1, T2);
  Demultiplexer demultiplexer_7 (
    .out0(demultiplexer_7_out0), .out1(F2), .in(demultiplexer_6_out0), .sel(a___b));  // open: en
  Demultiplexer demultiplexer_8 (.out0(demultiplexer_8_out0), .out1(restart2), .in(Output), .sel(start));  // open: en
  D_Flip_Flop TRUE (.clk(clk), .D(or_3_out), .Q(Output), .reset(reset));  // open: Qn, preset, en
  D_Flip_Flop WHILE (.clk(clk), .D(or_4_out), .Q(Sa), .reset(reset));  // open: Qn, preset, en
  or or_4 (or_4_out, demultiplexer_7_out0, demultiplexer_2_out0);
  or or_5 (END, END1, Output);
  or or_6 (La, Lb, Sa);

  // Other names for the same wires on the sheet: La0 = Lb; La1 = Sa; rst = reset; END2 = Output; TRUE = Output
endmodule

module Divisibility_2 (
  input  [31:0] A,
  input  [31:0] B,
  input  start,
  input  rst,
  input  clk,
  output Output,
  output END
);

  wire a___0, a___b, b___0, div_cu_1_la, div_cu_1_lb, div_cu_1_sa;

  Div_CU div_cu_1 (
    .a___0(a___0), .a___b(a___b), .b___0(b___0), .reset(rst), .start(start), .clk(clk), .Output(Output),
    .END(END), .Sa(div_cu_1_sa), .La(div_cu_1_la), .Lb(div_cu_1_lb));
  Div_DataP div_datap_1 (
    .Ain(A), .Bin(B), .Sa(div_cu_1_sa), .La(div_cu_1_la), .Lb(div_cu_1_lb), .A___0(a___0), .A___B(a___b),
    .B___0(b___0), .CLK(clk));
endmodule

module Test (
  input  [31:0] A,
  input  in_2,
  input  [31:0] B
);

  wire button_1_out, clock_1_out, divisibility_1_end, divisibility_1_output;

  // Probe on A
  // Probe on B
  Button button_1 (.out(button_1_out));
  Clock clock_1 (.out(clock_1_out));
  LED led_1 (.in(divisibility_1_end));
  Divisibility_2 divisibility_1 (
    .A(A), .B(B), .start(in_2), .rst(button_1_out), .clk(clock_1_out), .END(divisibility_1_end),
    .Output(divisibility_1_output));
  // Probe on divisibility_1_output
endmodule
